# Fritzing sketch wiring01_1 (saved by Fritzing 0.9.9b)

parts:
  M1 = Niren can bus module [package=THT]
  Bauteil1 = Arduino Nano (Rev3.0)
  Bauteil2 = FTDI Basic Programmer
  Bauteil3 = Current Sensor 5A
  Bauteil4 = Voltage Sensor 25V
  J1 = top view banana jack red [package=THT]
  J2 = top view banana jack red [package=THT]
  J3 = top view banana jack black [package=THT]  # not connected
  J4 = top view banana jack black [package=THT]

nets:
  VCC: M1.pin1, Bauteil1.5V, Bauteil3.1, Bauteil3.VCC, Bauteil4.VCC, Bauteil4.+, J1.pin1
  GND: M1.pin2, Bauteil1.GND, Bauteil2.GND, Bauteil3.GND, Bauteil4.-
  N1: M1.pin3, Bauteil1.D10
  N2: M1.pin4, Bauteil1.D12/MISO
  N3: M1.pin5, Bauteil1.D11/MOSI
  N4: M1.pin6, Bauteil1.D13/SCK
  N5: M1.pin7, Bauteil1.D2
  N6: Bauteil1.D1/TX, Bauteil2.RXI
  N7: Bauteil1.D0/RX, Bauteil2.TXO
  N8: Bauteil1.A1, Bauteil4.S
  N9: Bauteil1.A0, Bauteil3.2, Bauteil3.OUT, J2.pin1
  N10: Bauteil4.GND, J4.pin1

notes:
  IN OUT

custom parts:
  Niren can bus module: Niren can bus module availabe on ebay and others. Pcb view assumes that you unsolder the 7 pin header and resolder it on the bottom of the module to connect to the pcb. The two jumpers and the can bus connector remain on the top of the board and don't appear in pcb view.
  FTDI Basic Programmer: Description: This is the newest revision of our FTDI Basic. We now use a SMD 6-pin header on the bottom, which makes it smaller and more compact. Functionality has remained the same. This is a basic breakout board for the FTDI FT232RL USB to serial IC. The pinout of this board matches the FTDI cable to work with official Arduino and cloned 3.3V Arduino boards. It can also be used for general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
  top view banana jack red: Top view banana jack red.
  top view banana jack black: Top view banana jack black.
